// Logisim project 3_zad.circ as structural Verilog: 1 circuit, main circuit main
module main (
  input  X,
  input  Res,
  output Y
);

  wire CLK_out, J1_out, J2_out, J3_2_out, J3_out, j_k_ff_1_q, j_k_ff_1_qn, j_k_ff_2_q, j_k_ff_2_qn,
       j_k_ff_3_q, j_k_ff_3_qn, K1_out, K3_out, nand_1_out, nand_2_out, nand_3_out, nand_4_out, nand_5_out,
       Y_out;

  nand nand_1 (nand_1_out, X, X);
  Clock CLK (.out(CLK_out));
  nand J1 (J1_out, nand_1_out, j_k_ff_2_q, j_k_ff_3_q);
  nand K1 (K1_out, j_k_ff_3_q, X);
  nand J2 (J2_out, X, j_k_ff_1_qn, j_k_ff_3_q);
  nand J3 (J3_out, j_k_ff_2_q, nand_1_out);
  nand J3_2 (J3_2_out, j_k_ff_2_qn, X);
  nand K3 (K3_out, j_k_ff_2_qn, j_k_ff_1_qn);
  nand u_Y (Y_out, nand_1_out, j_k_ff_1_q, j_k_ff_2_q);
  nand nand_2 (nand_2_out, J1_out, J1_out);
  nand nand_3 (nand_3_out, J2_out, J2_out);
  nand nand_4 (nand_4_out, J3_out, j_k_ff_1_qn, J3_2_out);
  nand nand_5 (nand_5_out, X, K3_out);
  nand nand_6 (Y, Y_out, Y_out);
  J_K_Flip_Flop j_k_ff_1 (
    .J(nand_2_out), .clk(CLK_out), .K(K1_out), .Q(j_k_ff_1_q), .Qn(j_k_ff_1_qn), .reset(Res));  // open: preset, en
  J_K_Flip_Flop j_k_ff_2 (
    .J(nand_3_out), .clk(CLK_out), .K(j_k_ff_3_q), .Q(j_k_ff_2_q), .Qn(j_k_ff_2_qn), .reset(Res));  // open: preset, en
  J_K_Flip_Flop j_k_ff_3 (
    .J(nand_4_out), .clk(CLK_out), .K(nand_5_out), .Q(j_k_ff_3_q), .Qn(j_k_ff_3_qn), .reset(Res));  // open: preset, en

  // Notes on the sheet:
  //   Z1 !Z1 Z2 !Z2 Z3 !Z3
endmodule
